# Fritzing sketch elBanquos christmas light_MK1 (saved by Fritzing 0.9.3b)
breadboards: 1

parts:
  Bauteil1 = Arduino Uno (Rev3)
  LED_1_1 = ws2812b [package="smd 2812b"]
  J1 = male pin header, 3 pins [form="♂ (male)"]
  LED_1_2 = ws2812b [package="smd 2812b"]
  LED_1_3 = ws2812b [package="smd 2812b"]
  LED_1_4 = ws2812b [package="smd 2812b"]
  LED_1_5 = ws2812b [package="smd 2812b"]
  LED_1_6 = ws2812b [package="smd 2812b"]
  LED_1_7 = ws2812b [package="smd 2812b"]
  LED_1_8 = ws2812b [package="smd 2812b"]
  LED_2_8 = ws2812b [package="smd 2812b"]
  LED_2_5 = ws2812b [package="smd 2812b"]
  LED_2_4 = ws2812b [package="smd 2812b"]
  LED_2_2 = ws2812b [package="smd 2812b"]
  LED_2_7 = ws2812b [package="smd 2812b"]
  LED_2_3 = ws2812b [package="smd 2812b"]
  LED_2_6 = ws2812b [package="smd 2812b"]
  LED_2_1 = ws2812b [package="smd 2812b"]
  LED_3_4 = ws2812b [package="smd 2812b"]
  LED_3_7 = ws2812b [package="smd 2812b"]
  LED_3_2 = ws2812b [package="smd 2812b"]
  LED_3_1 = ws2812b [package="smd 2812b"]
  LED_3_6 = ws2812b [package="smd 2812b"]
  LED_3_3 = ws2812b [package="smd 2812b"]
  LED_3_8 = ws2812b [package="smd 2812b"]
  LED_3_5 = ws2812b [package="smd 2812b"]
  J2 = male pin header, 3 pins [form="♂ (male)"]
  J3 = male pin header, 3 pins [form="♂ (male)"]

nets:
  N1: Bauteil1.D10_PWM/SS, LED_3_1.DIN, J3.pin1
  N2: Bauteil1.D11_PWM/MOSI, LED_2_1.DIN, J2.pin1
  N3: Bauteil1.D12/MISO, LED_1_1.DIN, J1.pin1
  VSS: Bauteil1.GND, LED_1_1.VSS, J1.pin3, LED_1_2.VSS, LED_1_3.VSS, LED_1_4.VSS, LED_1_5.VSS, LED_1_6.VSS, LED_1_7.VSS, LED_1_8.VSS, LED_2_8.VSS, LED_2_5.VSS, LED_2_4.VSS, LED_2_2.VSS, LED_2_7.VSS, LED_2_3.VSS, LED_2_6.VSS, LED_2_1.VSS, LED_3_4.VSS, LED_3_7.VSS, LED_3_2.VSS, LED_3_1.VSS, LED_3_6.VSS, LED_3_3.VSS, LED_3_8.VSS, LED_3_5.VSS, J2.pin3, J3.pin3
  VDD: Bauteil1.5V, LED_1_1.VDD, J1.pin2, LED_1_2.VDD, LED_1_3.VDD, LED_1_4.VDD, LED_1_5.VDD, LED_1_6.VDD, LED_1_7.VDD, LED_1_8.VDD, LED_2_8.VDD, LED_2_5.VDD, LED_2_4.VDD, LED_2_2.VDD, LED_2_7.VDD, LED_2_3.VDD, LED_2_6.VDD, LED_2_1.VDD, LED_3_4.VDD, LED_3_7.VDD, LED_3_2.VDD, LED_3_1.VDD, LED_3_6.VDD, LED_3_3.VDD, LED_3_8.VDD, LED_3_5.VDD, J2.pin2, J3.pin2
  N4: LED_1_1.DOUT, LED_1_2.DIN
  N5: LED_1_2.DOUT, LED_1_3.DIN
  N6: LED_1_3.DOUT, LED_1_4.DIN
  N7: LED_1_4.DOUT, LED_1_5.DIN
  N8: LED_1_5.DOUT, LED_1_6.DIN
  N9: LED_1_6.DOUT, LED_1_7.DIN
  N10: LED_1_7.DOUT, LED_1_8.DIN
  N11: LED_2_8.DIN, LED_2_7.DOUT
  N12: LED_2_5.DOUT, LED_2_6.DIN
  N13: LED_2_5.DIN, LED_2_4.DOUT
  N14: LED_2_4.DIN, LED_2_3.DOUT
  N15: LED_2_2.DOUT, LED_2_3.DIN
  N16: LED_2_2.DIN, LED_2_1.DOUT
  N17: LED_2_7.DIN, LED_2_6.DOUT
  N18: LED_3_4.DOUT, LED_3_5.DIN
  N19: LED_3_4.DIN, LED_3_3.DOUT
  N20: LED_3_7.DOUT, LED_3_8.DIN
  N21: LED_3_7.DIN, LED_3_6.DOUT
  N22: LED_3_2.DOUT, LED_3_3.DIN
  N23: LED_3_2.DIN, LED_3_1.DOUT
  N24: LED_3_6.DIN, LED_3_5.DOUT

notes:
  Not modeled
  Cable piece
